// Logisim project XOR.circ as structural Verilog: 2 circuits, main circuit main
module main (
  input  B5,
  input  B4,
  input  B3,
  input  B2,
  input  B1,
  input  B0,
  output LED
);

  wire myxor_1_out_3, myxor_2_out_3, myxor_3_out_3, myxor_4_out_3;

  myXOR myxor_1 (.A(B5), .B(B4), .out_3(myxor_1_out_3));
  myXOR myxor_2 (.A(B3), .B(B2), .out_3(myxor_2_out_3));
  myXOR myxor_3 (.A(B1), .B(B0), .out_3(myxor_3_out_3));
  myXOR myxor_4 (.A(myxor_1_out_3), .B(myxor_2_out_3), .out_3(myxor_4_out_3));
  myXOR myxor_5 (.A(myxor_4_out_3), .B(myxor_3_out_3), .out_3(LED));
endmodule

module myXOR (
  input  A,
  input  B,
  output out_3
);

  wire and_1_out, and_2_out, not_1_out, not_2_out;

  not not_1 (not_1_out, A);
  not not_2 (not_2_out, B);
  and and_1 (and_1_out, A, not_2_out);
  and and_2 (and_2_out, not_1_out, B);
  or or_1 (out_3, and_1_out, and_2_out);
endmodule
